# Fritzing sketch netzfrequenz (saved by Fritzing 0.9.3b)

parts:
  microSD_Transflash = SparkFun - microSD Transflash
  Antenne_für_Netzfrequenzbrummen = Antenna
  Bauteil1 = Arduino Nano (Rev3.0) (ICSP)
  Debugled = LED - 5mm [color="Red (633nm)" package="5 mm [THT]"]
  R1 = Resistor [tolerance=±5% resistance=220 package=THT]

nets:
  N1: microSD_Transflash.DO, Bauteil1.D12/MISO
  GND: microSD_Transflash.GND, Bauteil1.GND, R1.Pin_1
  N2: microSD_Transflash.SCK, Bauteil1.D13/SCK
  3.3V: microSD_Transflash.VCC, Bauteil1.3V3
  N3: microSD_Transflash.DI, Bauteil1.D11/MOSI
  N4: microSD_Transflash.CS, Bauteil1.D10
  N5: Antenne_für_Netzfrequenzbrummen.antenna_lead, Bauteil1.A0
  N6: Bauteil1.D2, Debugled.anode
  N7: Debugled.cathode, R1.Pin_0

notes:
  MISO
  MOSI
  CLK
