# Fritzing sketch netzfrequenz_Aktiv (saved by Fritzing 0.9.3b)

parts:
  microSD_Transflash = SparkFun - microSD Transflash
  Bauteil1 = Arduino Nano (Rev3.0) (ICSP)
  Debugled = LED - 5mm [color="Red (633nm)" package="5 mm [THT]"]
  R1 = Resistor [tolerance=±5% resistance=220 package=THT]
  D1 = Rectifier Diode [part_number=1N4001 package="300 mil [THT]"]
  12V_AC = Inductor [package="400 mil [THT]"]
  D2 = Rectifier Diode [part_number=1N4001 package="300 mil [THT]"]
  R2 = Resistor [tolerance=±5% resistance=1k package=THT]
  LED1 = LED - 5mm [color="Blue (430nm)" package="5 mm [THT]"]

nets:
  N1: microSD_Transflash.DO, Bauteil1.D12/MISO
  GND: microSD_Transflash.GND, Bauteil1.GND, R1.Pin_1, D2.anode, R2.Pin_0, LED1.cathode
  N2: microSD_Transflash.SCK, Bauteil1.D13/SCK
  3.3V: microSD_Transflash.VCC, Bauteil1.3V3
  N3: microSD_Transflash.DI, Bauteil1.D11/MOSI
  N4: microSD_Transflash.CS, Bauteil1.D10
  N5: Bauteil1.D2, Debugled.anode
  N6: Bauteil1.A1, D1.cathode, D2.cathode, LED1.anode
  N7: Debugled.cathode, R1.Pin_0
  N8: D1.anode, 12V_AC.pin_0
  N9: 12V_AC.pin_1, R2.Pin_1

notes:
  MISO
  MOSI
  CLK
